// Logisim project miniac.circ as structural Verilog: 1 circuit, main circuit main
module main (
);

  wire and_1_out, Clock_out, nor_1_out, nor_2_out, undriven_2, undriven_4;
  wire [2:0] rom_1_data_2;
  wire [4:0] demultiplexer_1_out0, demultiplexer_1_out1, demultiplexer_1_out2, demultiplexer_1_out3,
       demultiplexer_1_out4, demultiplexer_1_out5, demultiplexer_1_out6, demultiplexer_1_out7, or_1_out,
       rom_1_data;
  wire [7:0] AC_q, adder_1_out, multiplexer_1_out, multiplexer_2_out, PC_q, ram_1_data, subtractor_1_out,
       undriven, undriven_3;

  Clock Clock (.out(Clock_out));
  Multiplexer #(.width(8)) multiplexer_1 (
    .in0(adder_1_out), .in1(undriven), .out(multiplexer_1_out), .sel(and_1_out));  // open: en
  Register PC (.D(multiplexer_1_out), .Q(PC_q), .clk(Clock_out));  // open: en, clr
  Multiplexer #(.width(8)) multiplexer_2 (
    .in0(AC_q), .in1(subtractor_1_out), .out(multiplexer_2_out), .sel(undriven_2));  // open: en
  Adder adder_1 (.a(PC_q), .b(8'h1), .out(adder_1_out));  // open: cin, cout
  and and_1 (and_1_out, nor_1_out, nor_2_out);
  Register AC (.D(multiplexer_2_out), .Q(AC_q), .clk(Clock_out));  // open: en, clr
  nor nor_1 (nor_1_out, rom_1_data_2[1], rom_1_data_2[2]);
  nor nor_2 (nor_2_out, AC_q[0], AC_q[1], AC_q[2], AC_q[3], AC_q[4], AC_q[5], AC_q[6], AC_q[7]);
  ROM rom_1 (.addr(PC_q), .data({rom_1_data_2, rom_1_data}));  // open: sel
  // Probe on {rom_1_data_2, rom_1_data}
  Subtractor subtractor_1 (.a(AC_q), .b(ram_1_data), .out(subtractor_1_out));  // open: bin, bout
  Demultiplexer #(.select(3), .width(5)) demultiplexer_1 (
    .out0(demultiplexer_1_out0), .out1(demultiplexer_1_out1), .out2(demultiplexer_1_out2),
    .out3(demultiplexer_1_out3), .out4(demultiplexer_1_out4), .out5(demultiplexer_1_out5),
    .out6(demultiplexer_1_out6), .out7(demultiplexer_1_out7), .in(rom_1_data), .sel(rom_1_data_2));  // open: en
  assign or_1_out = demultiplexer_1_out2;  // OR_Gate or_1, 5 bits wide OR_Gate
  RAM #(.addrWidth(5), .bus("separate")) ram_1 (
    .addr(or_1_out), .din(undriven_3), .data(ram_1_data), .str(undriven_4), .clk(Clock_out));  // open: sel, ld, clr

  // Notes on the sheet:
  //   Place your name(s) here.
  //   CSCI 230 Assn 8
  //   contents of rom_1 (hex, n*v repeats v):
  //   e1 ff af af bf 2f 6f
endmodule
